// Logisim project Project.circ as structural Verilog
module CPU (
  output out_1,
  output out_2,
  output out_3,
  output out_4
);

  wire button_1_out, CLK_out, controlunit_1_ain, controlunit_1_asen, controlunit_1_bin, controlunit_1_clear,
       controlunit_1_irin, counter_2_lsb, counter_2_msb, or_1_out;
  wire [1:0] controlunit_1_dinout;
  wire [2:0] controlunit_1_ryout_2;
  wire [3:0] B_q, B_q_2, R5_q, R5_q_2, R6_q, R6_q_2, R7_q, R7_q_2;
  wire [7:0] A_q, alu_1_out_4, controlunit_1_out_7, counter_1_q, multiplexer_1_out, multiplexer_2_out,
       multiplexer_3_out, multiplexer_4_out, R0_q, R1_q, R2_q, R3_q, R4_q, ram_1_data, register_1_q;

  Register R0 (.D(multiplexer_4_out), .en(controlunit_1_out_7[0]), .Q(R0_q), .clk(CLK_out), .clr(button_1_out));
  Counter_part counter_1 (
    .count(or_1_out), .Q(counter_1_q), .clk(CLK_out), .clr(button_1_out));  // open: load, D, carry
  Clock CLK (.out(CLK_out));
  Register R1 (.D(multiplexer_4_out), .en(controlunit_1_out_7[1]), .Q(R1_q), .clk(CLK_out), .clr(button_1_out));
  or or_1 (or_1_out, controlunit_1_irin, out_4);
  RAM ram_1 (.addr(counter_1_q), .data(ram_1_data), .clk(CLK_out));  // open: sel, ld, clr
  Register R2 (.D(multiplexer_4_out), .en(controlunit_1_out_7[2]), .Q(R2_q), .clk(CLK_out), .clr(button_1_out));
  Register R3 (.D(multiplexer_4_out), .en(controlunit_1_out_7[3]), .Q(R3_q), .clk(CLK_out), .clr(button_1_out));
  Multiplexer #(.select(3), .width(8)) multiplexer_1 (
    .in0(R0_q), .in1(R1_q), .in2(R2_q), .in3(R3_q), .in4(R4_q), .in5({R5_q_2, R5_q}), .in6({R6_q_2, R6_q}),
    .in7({R7_q_2, R7_q}), .out(multiplexer_1_out), .sel(controlunit_1_ryout_2));  // open: en
  Register register_1 (.D(ram_1_data), .en(controlunit_1_irin), .Q(register_1_q), .clk(CLK_out));  // open: clr
  Button button_1 (.out(button_1_out));
  Register R4 (.D(multiplexer_4_out), .en(controlunit_1_out_7[4]), .Q(R4_q), .clk(CLK_out), .clr(button_1_out));
  Multiplexer #(.width(8)) multiplexer_2 (
    .in1({B_q_2, B_q}), .out(multiplexer_2_out), .sel(controlunit_1_dinout[1]));  // open: in0, en
  Register R5 (
    .D(multiplexer_4_out), .en(controlunit_1_out_7[5]), .Q({R5_q_2, R5_q}), .clk(CLK_out), .clr(button_1_out));
  Multiplexer #(.width(8)) multiplexer_3 (
    .in1(ram_1_data), .out(multiplexer_3_out), .sel(controlunit_1_dinout[0]));  // open: in0, en
  Register R6 (
    .D(multiplexer_4_out), .en(controlunit_1_out_7[6]), .Q({R6_q_2, R6_q}), .clk(CLK_out), .clr(button_1_out));
  Multiplexer #(.select(2), .width(8)) multiplexer_4 (
    .in0(multiplexer_1_out), .in1(multiplexer_3_out), .in2(multiplexer_2_out), .out(multiplexer_4_out),
    .sel(controlunit_1_dinout));  // open: in3, en
  Register R7 (
    .D(multiplexer_4_out), .en(controlunit_1_out_7[7]), .Q({R7_q_2, R7_q}), .clk(CLK_out), .clr(button_1_out));
  Counter counter_2 (.Clear(controlunit_1_clear), .LSB(counter_2_lsb), .MSB(counter_2_msb), .Clock(CLK_out));
  Register A (.D(multiplexer_4_out), .en(controlunit_1_ain), .Q(A_q), .clk(CLK_out), .clr(button_1_out));
  ControlUnit controlunit_1 (
    .msb(counter_2_msb), .lsb(counter_2_lsb), .IR(register_1_q), .done(out_4), .Rxin(out_3), .Rxout(out_1),
    .Ryout(out_2), .Ain(controlunit_1_ain), .Ryout_2(controlunit_1_ryout_2), .Bin(controlunit_1_bin),
    .Bout(controlunit_1_dinout[1]), .Asen(controlunit_1_asen), .DINout(controlunit_1_dinout[0]),
    .IRin(controlunit_1_irin), .Reset(button_1_out), .Clear(controlunit_1_clear), .out_7(controlunit_1_out_7));
  Register B (.D(alu_1_out_4), .en(controlunit_1_bin), .Q({B_q_2, B_q}), .clk(CLK_out), .clr(button_1_out));
  Alu alu_1 (.Ain(A_q), .R0_R7(multiplexer_4_out), .out_4(alu_1_out_4), .Asen(controlunit_1_asen));
  Hex_Digit_Display hex_digit_display_1 (.value(R5_q));  // open: dp
  Hex_Digit_Display hex_digit_display_2 (.value(R5_q_2));  // open: dp
  Hex_Digit_Display hex_digit_display_3 (.value(R6_q_2));  // open: dp
  Hex_Digit_Display hex_digit_display_4 (.value(R6_q));  // open: dp
  Hex_Digit_Display hex_digit_display_5 (.value(R7_q_2));  // open: dp
  Hex_Digit_Display hex_digit_display_6 (.value(B_q_2));  // open: dp
  Hex_Digit_Display hex_digit_display_7 (.value(R7_q));  // open: dp
  Hex_Digit_Display hex_digit_display_8 (.value(B_q));  // open: dp

  // Notes on the sheet:
  //   Ra
  //   Rb
  //   Rc
endmodule

module Counter (
  input  Clock,
  input  Clear,
  output LSB,
  output MSB
);

  J_K_Flip_Flop j_k_ff_1 (.J(1'b1), .clk(Clock), .K(1'b1), .Q(LSB), .reset(Clear));  // open: Qn, preset, en
  J_K_Flip_Flop j_k_ff_2 (.J(LSB), .clk(Clock), .K(LSB), .Q(MSB), .reset(Clear));  // open: Qn, preset, en
endmodule

module Alu (
  input  [7:0] Ain,
  input  [7:0] R0_R7,
  input  Asen,
  output [7:0] out_4
);

  wire [7:0] adder_1_out, subtractor_1_out;

  Adder adder_1 (.a(Ain), .b(R0_R7), .out(adder_1_out));  // open: cin, cout
  Subtractor subtractor_1 (.a(Ain), .b(R0_R7), .out(subtractor_1_out));  // open: bin, bout
  Multiplexer #(.width(8)) multiplexer_1 (
    .in0(adder_1_out), .in1(subtractor_1_out), .out(out_4), .sel(Asen));  // open: en
endmodule

module ControlUnit (
  input  msb,
  input  lsb,
  input  Reset,
  input  [7:0] IR,
  output done,
  output Rxin,
  output [7:0] out_7,
  output Rxout,
  output Ryout,
  output Clear,
  output Ain,
  output [2:0] Ryout_2,
  output Bin,
  output Bout,
  output Asen,
  output DINout,
  output IRin
);

  wire and_1_out, and_2_out, and_3_out, and_4_out, and_5_out, and_6_out, and_7_out, and_8_out, and_9_out,
       and_12_out, and_13_out, and_14_out, and_15_out, and_17_out, and_18_out, and_20_out, and_21_out,
       not_1_out, not_2_out, not_3_out, not_4_out, not_5_out, not_6_out, not_7_out, not_8_out, not_9_out,
       not_10_out, not_11_out, not_12_out, not_13_out, not_14_out, or_1_out;

  Decoder #(.select(3), .disabled(0)) decoder_1 (
    .out0(out_7[0]), .out1(out_7[1]), .out2(out_7[2]), .out3(out_7[3]), .out4(out_7[4]), .out5(out_7[5]),
    .out6(out_7[6]), .out7(out_7[7]), .sel(IR[5:3]), .en(done));
  Multiplexer #(.select(2), .width(3)) multiplexer_1 (
    .in1(IR[2:0]), .in2(IR[5:3]), .out(Ryout_2), .sel({Rxout, Ryout}), .en(or_1_out));  // open: in0, in3
  or or_1 (or_1_out, Ryout, Rxout);
  not not_1 (not_1_out, IR[7]);
  not not_2 (not_2_out, msb);
  not not_3 (not_3_out, msb);
  not not_4 (not_4_out, IR[7]);
  not not_5 (not_5_out, IR[6]);
  not not_6 (not_6_out, msb);
  not not_7 (not_7_out, msb);
  and and_1 (and_1_out, IR[7], msb);
  not not_8 (not_8_out, lsb);
  and and_2 (and_2_out, IR[7], msb);
  not not_9 (not_9_out, lsb);
  not not_10 (not_10_out, IR[7]);
  not not_11 (not_11_out, msb);
  not not_12 (not_12_out, msb);
  not not_13 (not_13_out, lsb);
  and and_3 (and_3_out, not_1_out, not_2_out);
  and and_4 (and_4_out, IR[7], msb);
  and and_5 (and_5_out, IR[7], not_3_out);
  and and_6 (and_6_out, not_4_out, not_5_out);
  and and_7 (and_7_out, not_6_out, lsb);
  and and_8 (and_8_out, IR[7], msb);
  not not_14 (not_14_out, lsb);
  and and_9 (and_9_out, IR[7], not_7_out);
  and and_10 (Bin, and_1_out, not_8_out);
  and and_11 (Bout, and_2_out, lsb);
  and and_12 (and_12_out, IR[7], IR[6]);
  and and_13 (and_13_out, msb, not_9_out);
  and and_14 (and_14_out, not_10_out, IR[6]);
  and and_15 (and_15_out, not_11_out, lsb);
  and and_16 (IRin, not_12_out, not_13_out);
  and and_17 (and_17_out, and_3_out, lsb);
  or or_2 (done, and_17_out, and_18_out);
  and and_18 (and_18_out, and_4_out, lsb);
  and and_19 (Rxout, and_5_out, lsb);
  and and_20 (and_20_out, and_6_out, and_7_out);
  or or_3 (Ryout, and_20_out, and_21_out);
  and and_21 (and_21_out, and_8_out, not_14_out);
  and and_22 (Ain, and_9_out, lsb);
  and and_23 (Asen, and_12_out, and_13_out);
  and and_24 (DINout, and_14_out, and_15_out);

  assign Clear = Reset;
  assign Rxin = done;
endmodule
